# Fritzing sketch sketch (saved by Fritzing 0.9.3b)

parts:
  Part1 = Arduino Mega 2560 (Rev3)
  U4 = SUP500F [package=sup500f]
  Grove1 = Grove 3 Axis Digital Accelerometer 16g
  Part2 = Arduino Board Ethernet

nets:
  N1: Part1.D21/SCL, Grove1.SCL
  N2: Part1.D20/SDA, Grove1.SDA
  GND: Part1.GND, Grove1.GND
  N3: Part1.D13_PWM, Part2.D13/SCK
  N4: Part1.D12_PWM, Part2.D12/MISO
  N5: Part1.D11_PWM, Part2.D11/MOSI
  N6: Part1.D10_PWM, Part2.D10_PWM/SS
  5V: Part1.5V, Grove1.VCC
  N7: Part1.D0_RX0, U4.TX-O
  N8: Part1.D1_TX0, U4.RX-I
